# Fritzing sketch rpi-pir-sensor (saved by Fritzing 0.9.2b)

parts:
  Raspberry_Pi1 = Raspberry Pi B+
  PIR1 = PIR sensor

nets:
  GND: Raspberry_Pi1.GND, PIR1.GND
  N1: Raspberry_Pi1.GPIO21, PIR1.SIG
  5V: Raspberry_Pi1.5V, PIR1.VDD
